# Fritzing sketch sketch (saved by Fritzing 1.0.4)

parts:
  U2 = ESP8266 ESP-01 Upgraded WiFi Module [part_number=ESP8266]
  U1 = WS2815RGB LED strip
  U3 = Voltage Regulator - 5V [package="TO220 [THT]"]
  Power_plug1 = Power plug

nets:
  N1: U2.VCC, U3.output_voltage
  N2: U2.GPIO_0, U1.BI
  N3: U2.GPIO_2, U1.DI
  GND: U1.GND1, U3.GND, Power_plug1.GND
  N4: U3.input_voltage, Power_plug1.VCC

custom parts:
  ESP8266 ESP-01 Upgraded WiFi Module: Upgraded Version ESP-01,all Flash are upgraded to 1M byte.Also support Cloud service remote transmission.
  WS2815RGB LED strip: WS2815 RGBCI 12V strip
  Power plug: power plug
